# Fritzing sketch ASimpleIoTCircuitDiagram (saved by Fritzing 0.9.2b)
breadboards: 1

parts:
  LED1 = RGB LED (com. cathode, rbg) [package="5 mm [THT]"]
  IC1 = Single-Chip USB to UART Bridge [package=mlp28]
  R1 = Resistor [tolerance=±5% resistance=220 package=THT]
  R2 = Resistor [tolerance=±5% resistance=220 package=THT]
  R3 = Resistor [tolerance=±5% resistance=220 package=THT]
  S1 = Pushbutton [package="[THT]"]
  R4 = Resistor [tolerance=±5% resistance=10k package=THT]
  T1 = TMP36 Temperature Sensor [package="TO92 [THT]"]
  R5 = Resistor [tolerance=±5% resistance=220 package="0402 [SMD]"]
  D1 = LTE-302 [package=lte-302]
  D2 = LTE-302 [package=lte-302]
  D4 = LTE-302 [package=lte-302]
  D5 = Diode [package=diode-1n4001]  # not connected
  U1 = Optocoupler [package=THT]

nets:
  N1: LED1.red_anode, R1.Pin_0
  GND: LED1.common_cathode, IC1.GND, S1.Pin_1, S1.Pin_2, R4.Pin_0, T1.GND, U1.Pin_2
  N2: LED1.blue_anode, R2.Pin_0
  N3: LED1.green_anode, R3.Pin_0
  N4: IC1.RI, T1.+Vs
  N5: IC1.!SUSPEND, R3.Pin_1, S1.Pin_3, S1.Pin_4
  N6: IC1.GPIO_3, T1.Vout
  N7: R5.Pin_1, U1.Pin_1
  N8: D1.A, D2.C
  N9: D2.A, D4.C
  N10: D4.A, U1.Pin_5

notes:
  ESP8266-12E
  D1 - Blue (On/Off Switch, subscriber)
  D2 - Red (Slider, subscriber)
  D3 - Subscriber of Blue LED switch also triggers the Christmas Lights via optocoupler
  D4 - Green (Physical button, publisher)
  GND
  3V3
  220 Ω
  10k Ω
  TMP36,
  Temperature sensor
  An illustration of
  Christmas lights
  Power Adapter
  230 VAC
  to
  24 V DC
  Optocoupler
